# Fritzing sketch  Riego v2 (saved by Fritzing 0.9.3b)
breadboards: 1

parts:
  Componente3 = FC-28 Soil Hygrometer Module - Probe
  Componente4 = FC-28 Soil Hygrometer Module
  U1 = 4-Channel 5v Relay Shield [package=relay-4ch5v10a]
  M1 = DC Motor
  VCC1 = Battery
  R1 = Rotary Potentiometer (Small) [maximum_resistance=100kΩ package=THT]
  Componente5 = Arduino Uno (Rev3)
  Componente6 = LCD1602-I2C

nets:
  N1: Componente3.POS, Componente4.POS
  N2: Componente3.NEG, Componente4.NEG
  VCC: Componente4.VCC, U1.VCC, R1.leg1, Componente5.5V, Componente6.VCC
  GND: Componente4.GND, U1.GND, R1.leg2, Componente5.GND, Componente6.GND
  N3: Componente4.AO, Componente5.A0
  N4: U1.IN1, Componente5.D10_PWM/SS
  N5: U1.K4-Off, VCC1.-
  N6: U1.K4-On, M1.pin_2
  N7: R1.wiper, Componente5.A1
  N8: Componente5.A4/SDA, Componente6.SDA
  N9: Componente5.A5/SCL, Componente6.SCL

custom parts:
  FC-28 Soil Hygrometer Module - Probe: The FC-28 is a soil hygrometer module that uses the Texas Instruments LM393 comparator chip to provide an analog measurement of soil humidity.
  FC-28 Soil Hygrometer Module: The FC-28 is a soil hygrometer module that uses the Texas Instruments LM393 comparator chip to provide an analog measurement of soil humidity. The digital output is high when soil moisture is over a certain threshold, as determined by adjusting the potentiometer.
  4-Channel 5v Relay Shield: 4 Channel 5v Relay Shield w. 2x SPD-06VDC-SD-C
  LCD1602-I2C: A standard character display, usually with 2x16 characters. Comes in many colors with LCM1602 IIC attached.
