# Fritzing sketch 7.2 Pulsador pullDown (saved by Fritzing 0.9.3b)
breadboards: 1

parts:
  S1 = Pushbutton [package="[THT]"]
  Componente1 = Arduino Uno (Rev3)
  R1 = Resistor [tolerance=±5% resistance=10k package=THT]

nets:
  N1: S1.Pin_1, S1.Pin_2, Componente1.D2, R1.Pin_0
  N2: S1.Pin_3, S1.Pin_4, Componente1.5V
  N3: Componente1.GND, R1.Pin_1
