# Fritzing sketch 7.9.1 LM35 (saved by Fritzing 0.9.3b)
breadboards: 1

parts:
  part = Arduino Uno (Rev3)
  part_2 = LM35 Temperature Sensor [package="TO92 [THT]"]

nets:
  N1: part.A0, part_2.Vout
  GND: part.GND, part_2.GND
  N2: part.5V, part_2.+Vs
